# Fritzing sketch uno (saved by Fritzing 0.9.3b)
breadboards: 1

parts:
  부품1 = Arduino Uno (Rev3)
  BT2 = Bluetooth HC-06u [package=THT]

nets:
  N1: 부품1.D2, BT2.TXD
  N2: 부품1.D3_PWM, BT2.RXD
  3V3: 부품1.3V3, BT2.VCC
  GND: 부품1.GND, BT2.GND

custom parts:
  Bluetooth HC-06u: Bluetooth HC-06 - face up, pins down 16.5mm x 37.5mm PCB
